# Fritzing sketch sur24 (saved by Fritzing 0.9.3b)
perfboards: 1

parts:
  A1 = A9G GSM/GPRS+GPS Module
  M1 = DOIT Esp32 DevKit v1 (30 pins long, 11 pins width) [part_number=ESP32S-PIN30]
  J1 = Camdenboss CTB0158-2 [part_number=CTB0158-2 package=THT]
  OLED_I2C1 = OLED 128x64 I2C Monochrome Display  # not connected
  J2 = Camdenboss CTB0158-4 [part_number=CTB0158-4 package=THT]
  J3 = Camdenboss CTB0158-5 [part_number=CTB0158-5 package=THT]
  R1 = Resistor [tolerance=±5% resistance=10k package=THT]
  R2 = Resistor [tolerance=±5% resistance=10k package=THT]  # not connected
  R3 = Resistor [tolerance=±5% resistance=10k package=THT]  # not connected
  R4 = Resistor [tolerance=±5% resistance=10k package=THT]
  Q1 = Basic FET N-Channel [package="D2Pak [SMD]"]
  Q2 = Basic FET N-Channel [package="D2Pak [SMD]"]
  U1 = Optocoupler [package=THT]
  J4 = Camdenboss CTB0158-2 [part_number=CTB0158-2 package=THT]

nets:
  N1: A1.Pin_3, A1.Pin_28
  N2: A1.Pin_4, A1.Pin_5, A1.Pin_27, M1.GND, J1.pin1, Q2.source
  N3: A1.Pin_6, M1.VIN, J1.pin2, J2.pin1
  N4: A1.Pin_17, M1.TX2
  N5: A1.Pin_18, M1.RX2
  N6: M1.3V3, R1.Pin_1, R4.Pin_1
  N7: M1.D4, J3.pin2
  N8: M1.D5, J3.pin3
  N9: M1.D18, J3.pin4
  N10: M1.D19, J3.pin5
  N11: M1.D23, U1.Pin_1
  N12: M1.D14, Q2.Gate
  N13: M1.D13, Q1.Gate
  N14: J2.pin2, Q1.drain
  N15: J2.pin4, Q2.drain
  N16: J3.pin1, Q1.source
  N17: U1.Pin_4, J4.pin2
  N18: U1.Pin_5, J4.pin1

notes:
  sw SMS
  sw Alarma
  sw Izq
  sw Dcha
  GND switches
  GND Izq
  +5v Izq
  GND Dcha
  +5v Dcha
  GND
  5v Vin
  sw Sirena

custom parts:
  A9G GSM/GPRS+GPS Module: A9G is a complete quad-band GSM/GPRS+GPS module based on the RDA8955 chip.
  DOIT Esp32 DevKit v1 (30 pins long, 11 pins width): The DOIT Esp32 DevKit v1 is one of the development board created by DOIT to evaluate the ESP-WROOM-32 module. It is based on the ESP32 microcontroller that boasts Wifi, Bluetooth, Ethernet and Low Power support all in a single chip. (vanepp) made breadboard work, adjusted pin numbering and labels and reduced size of schematic and cleaned up pcb. This chip is 30pins long (2 x15) and 11 pins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
